// Logisim project Tic-Tac-Toe.circ as structural Verilog: 1 circuit, main circuit main
module main (
);

  wire and_2_out, and_3_out, and_4_out, and_5_out, and_6_out, and_7_out, and_8_out, and_9_out, and_10_out,
       and_11_out, B1, B2, B3, B4, B5, B6, B7, B8, B9, button_1_out, cdm_8_1_p2, cdm_8_1_p4, cdm_8_1_p5,
       cdm_8_1_p6, cdm_8_1_p7, cdm_8_1_p8, cdm_8_1_p9, cl, code, data, decoder_2_out0, decoder_2_out1,
       decoder_3_out0, decoder_3_out1, decoder_4_out0, decoder_4_out1, I_Osel, in_out, mem, nor_1_out,
       nor_2_out, not_1_out, not_2_out, not_3_out, not_5_out, not_6_out, rs_latch_1_q_prime, transistor_1_out;
  wire [1:0] CurrInput;
  wire [2:0] PageNum;
  wire [3:0] controlled_buffer_4_out, displayreg1_1_value, displayreg2_1_value, displayreg3_1_value,
       displayreg4_1_value, displayreg5_1_value, displayreg6_1_value, displayreg7_1_value,
       displayreg8_1_value, displayreg9_1_value, pull_resistor_4_node, random_1_out, register_4_q;
  wire [7:0] addr, cdm_8_1_p15, cdm_8_1_p16, codeData, dataData, demultiplexer_1_out2, I_Odat, register_1_q,
       register_2_q, register_3_q, rom_1_data, rom_2_data;
  wire [7:7] not_4_out;
  wire [8:0] _11, _12, _13, _14, _15, _21, _22, _23, _24, _25, _31, _32, _33, _34, _35, _41, _42, _43, _44,
       _45, _51, _52, _53, _54, _55, _61, _62, _63, _64, _65, _71, _72, _73, _74, _75, _81, _82, _83, _84,
       _85, _91, _92, _93, _94, _95;

  DotMatrix #(.matrixcols(9), .matrixrows(9)) dotmatrix_1 (
    .col0(_11), .col1(_12), .col2(_13), .col3(_14), .col4(_15), .col5(_14), .col6(_13), .col7(_12), .col8(_11));
  DotMatrix #(.matrixcols(9), .matrixrows(9)) dotmatrix_2 (
    .col0(_41), .col1(_42), .col2(_43), .col3(_44), .col4(_45), .col5(_44), .col6(_43), .col7(_42), .col8(_41));
  DotMatrix #(.matrixcols(9), .matrixrows(9)) dotmatrix_3 (
    .col0(_71), .col1(_72), .col2(_73), .col3(_74), .col4(_75), .col5(_74), .col6(_73), .col7(_72), .col8(_71));
  // Probe on cdm_8_1_p2
  Button button_1 (.out(button_1_out));
  Clock clock_1 (.out(cl));
  Pull_Resistor pull_resistor_1 (.node(I_Odat));
  // Probe on cdm_8_1_p4
  // Probe on cdm_8_1_p6
  // Probe on cdm_8_1_p5
  and and_1 (CurrInput[1], addr[4], addr[5], addr[6], addr[7]);
  DotMatrix #(.matrixcols(9), .matrixrows(9)) dotmatrix_4 (
    .col0(_21), .col1(_22), .col2(_23), .col3(_24), .col4(_25), .col5(_24), .col6(_23), .col7(_22), .col8(_21));
  DotMatrix #(.matrixcols(9), .matrixrows(9)) dotmatrix_5 (
    .col0(_51), .col1(_52), .col2(_53), .col3(_54), .col4(_55), .col5(_54), .col6(_53), .col7(_52), .col8(_51));
  DotMatrix #(.matrixcols(9), .matrixrows(9)) dotmatrix_6 (
    .col0(_81), .col1(_82), .col2(_83), .col3(_84), .col4(_85), .col5(_84), .col6(_83), .col7(_82), .col8(_81));
  // Probe on cdm_8_1_p9
  // Probe on cdm_8_1_p7
  // Probe on cdm_8_1_p8
  DotMatrix #(.matrixcols(9), .matrixrows(9)) dotmatrix_7 (
    .col0(_31), .col1(_32), .col2(_33), .col3(_34), .col4(_35), .col5(_34), .col6(_33), .col7(_32), .col8(_31));
  DotMatrix #(.matrixcols(9), .matrixrows(9)) dotmatrix_8 (
    .col0(_61), .col1(_62), .col2(_63), .col3(_64), .col4(_65), .col5(_64), .col6(_63), .col7(_62), .col8(_61));
  DotMatrix #(.matrixcols(9), .matrixrows(9)) dotmatrix_9 (
    .col0(_91), .col1(_92), .col2(_93), .col3(_94), .col4(_95), .col5(_94), .col6(_93), .col7(_92), .col8(_91));
  Decoder #(.select(2), .disabled(0)) decoder_1 (
    .out0(code), .out1(data), .out3(I_Osel), .sel(CurrInput), .en(mem));  // open: out2
  Pull_Resistor pull_resistor_2 (.node(addr));
  // CdM_8 cdm_8_1: pin names not known; wires that end beside it: cl, cdm_8_1_p2, button_1_out, cdm_8_1_p4, cdm_8_1_p5, cdm_8_1_p6, cdm_8_1_p7, cdm_8_1_p8, cdm_8_1_p9, CurrInput[0], mem, in_out, PageNum, addr, cdm_8_1_p15, cdm_8_1_p16
  and and_2 (and_2_out, ~in_out, mem);  // AND_Gate
  LED Player (.in(and_3_out));
  and and_3 (and_3_out, register_2_q[0], register_2_q[1]);
  Demultiplexer #(.select(2), .width(8)) demultiplexer_1 (
    .out1(dataData), .out2(demultiplexer_1_out2), .out3(I_Odat), .in(cdm_8_1_p15), .sel(CurrInput),
    .en(and_2_out));  // open: out0
  Multiplexer #(.select(2), .width(8)) multiplexer_1 (
    .in0(codeData), .in1(dataData), .in3(I_Odat), .out(cdm_8_1_p16), .sel(CurrInput), .en(and_4_out));  // open: in2
  and and_4 (and_4_out, in_out, mem);
  Button button_2 (.out(B1));
  Button button_3 (.out(B4));
  Button button_4 (.out(B7));
  LED Computer (.in(and_5_out));
  and and_5 (and_5_out, ~register_2_q[0], register_2_q[1]);  // AND_Gate
  // Probe on PageNum
  Button button_5 (.out(B3));
  Button button_6 (.out(B2));
  Button button_7 (.out(B5));
  Button button_8 (.out(B6));
  Button button_9 (.out(B9));
  Button button_10 (.out(B8));
  assign I_Odat = decoder_2_out1 ? register_2_q : 8'bz;  // Controlled_Buffer controlled_buffer_1
  Register register_1 (.D(I_Odat), .Q(register_1_q), .clk(decoder_3_out0));  // open: en, clr
  assign I_Odat = decoder_3_out1 ? register_1_q : 8'bz;  // Controlled_Buffer controlled_buffer_2
  and and_6 (and_6_out, addr[3], addr[2], ~addr[1], ~addr[0], I_Osel);  // AND_Gate
  Decoder #(.disabled(0)) decoder_2 (.out0(decoder_2_out0), .out1(decoder_2_out1), .sel(in_out), .en(and_6_out));
  Register register_2 (.D(I_Odat), .Q(register_2_q), .clk(decoder_2_out0));  // open: en, clr
  ROM rom_1 (.addr(addr), .data(rom_1_data), .sel(code));
  ROM rom_2 (.addr(addr), .data(rom_2_data), .sel(code));
  RAM ram_1 (.addr(addr), .data(dataData), .sel(data), .clk(cl), .ld(in_out));  // open: clr
  and and_7 (and_7_out, addr[3], addr[2], addr[1], addr[0], I_Osel);
  Decoder #(.disabled(0)) decoder_3 (.out0(decoder_3_out0), .out1(decoder_3_out1), .sel(in_out), .en(and_7_out));
  Multiplexer #(.width(8), .disabled(0), .enable("false")) multiplexer_2 (
    .in0(rom_1_data), .in1(rom_2_data), .out(codeData), .sel(PageNum[0]));
  assign I_Odat = decoder_4_out1 ? register_3_q : 8'bz;  // Controlled_Buffer controlled_buffer_3
  and and_8 (and_8_out, addr[3], addr[2], addr[1], ~addr[0], I_Osel);  // AND_Gate
  Decoder #(.disabled(0)) decoder_4 (.out0(decoder_4_out0), .out1(decoder_4_out1), .sel(in_out), .en(and_8_out));
  Register register_3 (.D(I_Odat), .Q(register_3_q), .clk(decoder_4_out0));  // open: en, clr
  assign controlled_buffer_4_out = B1 ? 4'b0001 : 4'bz;  // Controlled_Buffer controlled_buffer_4
  not not_1 (not_1_out, transistor_1_out);
  DisplayReg1 displayreg1_1 (
    .in_out(in_out), .I_Odat(I_Odat[3:0]), .value(displayreg1_1_value), .I_Oadr(addr[3:0]), .I_Osel(I_Osel),
    .out(I_Odat[3:0]));
  Transistor #(.\type ("n")) transistor_1 (.in(1'b0), .out(transistor_1_out), .gate(B2));
  Transistor #(.\type ("n")) transistor_2 (.in(1'b0), .out(transistor_1_out), .gate(B1));
  assign controlled_buffer_4_out = B2 ? 4'b0010 : 4'bz;  // Controlled_Buffer controlled_buffer_5
  assign controlled_buffer_4_out = B3 ? 4'b0011 : 4'bz;  // Controlled_Buffer controlled_buffer_6
  not not_2 (not_2_out, not_1_out);
  not not_3 (not_3_out, and_11_out);
  DisplayReg2 displayreg2_1 (
    .in_out(in_out), .I_Odat(I_Odat[3:0]), .value(displayreg2_1_value), .I_Oadr(addr[3:0]), .I_Osel(I_Osel),
    .out(I_Odat[3:0]));
  DisplayReg3 displayreg3_1 (
    .in_out(in_out), .I_Odat(I_Odat[3:0]), .value(displayreg3_1_value), .I_Oadr(addr[3:0]), .I_Osel(I_Osel),
    .out(I_Odat[3:0]));
  Transistor #(.\type ("n")) transistor_3 (.in(1'b0), .out(transistor_1_out), .gate(B3));
  Transistor #(.\type ("n")) transistor_4 (.in(1'b0), .out(transistor_1_out), .gate(B4));
  assign controlled_buffer_4_out = B5 ? 4'b0101 : 4'bz;  // Controlled_Buffer controlled_buffer_7
  assign controlled_buffer_4_out = B4 ? 4'b0100 : 4'bz;  // Controlled_Buffer controlled_buffer_8
  nor nor_1 (nor_1_out, not_1_out, not_2_out);
  nor nor_2 (nor_2_out, and_11_out, not_3_out);
  DisplayReg4 displayreg4_1 (
    .in_out(in_out), .I_Odat(I_Odat[3:0]), .value(displayreg4_1_value), .I_Oadr(addr[3:0]), .I_Osel(I_Osel),
    .out(I_Odat[3:0]));
  DisplayControl displaycontrol_1 (
    .\input (displayreg1_1_value), .outSignals_1_2({_12, _11}), .outSignals_3_4_5({_15, _14, _13}));
  DisplayControl displaycontrol_2 (
    .\input (displayreg3_1_value), .outSignals_1_2({_32, _31}), .outSignals_3_4_5({_35, _34, _33}));
  DisplayControl displaycontrol_3 (
    .\input (displayreg2_1_value), .outSignals_1_2({_22, _21}), .outSignals_3_4_5({_25, _24, _23}));
  Transistor #(.\type ("n")) transistor_5 (.in(1'b0), .out(transistor_1_out), .gate(B5));
  Transistor #(.\type ("n")) transistor_6 (.in(1'b0), .out(transistor_1_out), .gate(B6));
  assign controlled_buffer_4_out = B7 ? 4'b0111 : 4'bz;  // Controlled_Buffer controlled_buffer_9
  assign controlled_buffer_4_out = B6 ? 4'b0110 : 4'bz;  // Controlled_Buffer controlled_buffer_10
  RS_latch rs_latch_1 (.S(nor_1_out), .R(nor_2_out), .Q_prime(rs_latch_1_q_prime));  // open: Q, reset
  not not_4 (not_4_out[7], rs_latch_1_q_prime);
  DisplayReg5 displayreg5_1 (
    .in_out(in_out), .I_Odat(I_Odat[3:0]), .value(displayreg5_1_value), .I_Oadr(addr[3:0]), .I_Osel(I_Osel),
    .out(I_Odat[3:0]));
  DisplayControl displaycontrol_4 (
    .\input (displayreg6_1_value), .outSignals_1_2({_62, _61}), .outSignals_3_4_5({_65, _64, _63}));
  DisplayControl displaycontrol_5 (
    .\input (displayreg4_1_value), .outSignals_1_2({_42, _41}), .outSignals_3_4_5({_45, _44, _43}));
  DisplayControl displaycontrol_6 (
    .\input (displayreg5_1_value), .outSignals_1_2({_52, _51}), .outSignals_3_4_5({_55, _54, _53}));
  Transistor #(.\type ("n")) transistor_7 (.in(1'b0), .out(transistor_1_out), .gate(B8));
  Transistor #(.\type ("n")) transistor_8 (.in(1'b0), .out(transistor_1_out), .gate(B7));
  assign controlled_buffer_4_out = B8 ? 4'b1000 : 4'bz;  // Controlled_Buffer controlled_buffer_11
  assign controlled_buffer_4_out = B9 ? 4'b1001 : 4'bz;  // Controlled_Buffer controlled_buffer_12
  DisplayReg6 displayreg6_1 (
    .in_out(in_out), .I_Odat(I_Odat[3:0]), .value(displayreg6_1_value), .I_Oadr(addr[3:0]), .I_Osel(I_Osel),
    .out(I_Odat[3:0]));
  DisplayReg7 displayreg7_1 (
    .in_out(in_out), .I_Odat(I_Odat[3:0]), .value(displayreg7_1_value), .I_Oadr(addr[3:0]), .I_Osel(I_Osel),
    .out(I_Odat[3:0]));
  DisplayControl displaycontrol_7 (
    .\input (displayreg8_1_value), .outSignals_1_2({_82, _81}), .outSignals_3_4_5({_85, _84, _83}));
  DisplayControl displaycontrol_8 (
    .\input (displayreg7_1_value), .outSignals_1_2({_72, _71}), .outSignals_3_4_5({_75, _74, _73}));
  not not_5 (not_5_out, transistor_1_out);
  Pull_Resistor #(.pull(1)) pull_resistor_3 (.node(transistor_1_out));
  Transistor #(.\type ("n")) transistor_9 (.in(1'b0), .out(transistor_1_out), .gate(B9));
  DisplayReg8 displayreg8_1 (
    .in_out(in_out), .I_Odat(I_Odat[3:0]), .value(displayreg8_1_value), .I_Oadr(addr[3:0]), .I_Osel(I_Osel),
    .out(I_Odat[3:0]));
  DisplayControl displaycontrol_9 (
    .\input (displayreg9_1_value), .outSignals_1_2({_92, _91}), .outSignals_3_4_5({_95, _94, _93}));
  not not_6 (not_6_out, not_5_out);
  Register #(.width(4), .trigger("falling")) register_4 (
    .D(controlled_buffer_4_out), .Q(register_4_q), .clk(not_6_out));  // open: en, clr
  Pull_Resistor pull_resistor_4 (.node(pull_resistor_4_node));
  DisplayReg9 displayreg9_1 (
    .in_out(in_out), .I_Odat(I_Odat[3:0]), .value(displayreg9_1_value), .I_Oadr(addr[3:0]), .I_Osel(I_Osel),
    .out(I_Odat[3:0]));
  and and_9 (and_9_out, I_Osel, addr[0], addr[1], ~addr[2], addr[3], in_out);  // AND_Gate
  Random #(.width(4), .seed(123)) random_1 (.clk(cl), .out(random_1_out));  // open: next, clr
  assign I_Odat = and_11_out ? {{4{not_4_out[7]}}, register_4_q} : 8'bz;  // Controlled_Buffer controlled_buffer_13
  assign I_Odat[3:0] = and_9_out ? random_1_out : 4'bz;  // Controlled_Buffer controlled_buffer_14
  assign I_Odat[7:4] = and_9_out ? 4'b0000 : 4'bz;  // Controlled_Buffer controlled_buffer_15
  and and_10 (and_10_out, ~addr[0], addr[1], ~addr[2], addr[3], I_Osel);  // AND_Gate
  and and_11 (and_11_out, and_10_out, in_out);

  // Other names for the same wires on the sheet: I_OData[7:0] = I_Odat; I_Oadr[3:0] = addr[3:0];
  //   I_OSet = CurrInput[1]; rd_rw = in_out

  // Notes on the sheet:
  //   Page number
  //   PS saver
  //   contents of rom_1 (hex, n*v repeats v):
  //   0 d0 fa b1 5 e5 3 b7 f e1 1 d2 3 a6 db 10 d0 fb b2 d3 9 7e e4 10 a ed 10 d3 f0 5e bb f e1 10 d3 2 ab
  //   ee 1 d4
  //   contents of rom_2 (hex, n*v repeats v):
  //   d1 b d2 c d9 db 10 d4
  //   Page number
  //   Input controller
  //   3
  //   2
  //   1
  //   5
  //   6
  //   4
  //   Random generator
  //   I/O Adr: 11111011
  //   I/O Adr: 11111010
  //   7
  //   8
  //   9
  //   Screen data setters
  //   Screen choosers
endmodule
