// Logisim project Tic-Tac-Toe_Modules.circ as structural Verilog: 13 circuits, main circuit DisplayReg1
module DisplayControl (
  input  [3:0] \input ,
  output [17:0] outSignals_1_2,
  output [26:0] outSignals_3_4_5
);

  Multiplexer #(.width(18), .disabled(0)) multiplexer_1 (
    .in0(18'h202fe), .in1(18'h10501), .out(outSignals_1_2), .sel(\input [0]), .en(\input [1]));
  Pull_Resistor pull_resistor_1 (.node(outSignals_1_2));
  Multiplexer #(.width(27), .disabled(0)) multiplexer_2 (
    .in0(27'h4060301), .in1(27'h405044), .out(outSignals_3_4_5), .sel(\input [0]), .en(\input [1]));
  Pull_Resistor pull_resistor_2 (.node(outSignals_3_4_5));
endmodule

module DisplayReg1 (
  input  I_Osel,
  input  [3:0] I_Oadr,
  input  in_out,
  input  [3:0] I_Odat,
  output [3:0] out,
  output [3:0] value
);

  wire and_1_out, decoder_1_out0, decoder_1_out1;

  Register #(.width(4)) register_1 (.D(I_Odat), .Q(value), .clk(decoder_1_out0));  // open: en, clr
  assign out = decoder_1_out1 ? value : 4'bz;  // Controlled_Buffer controlled_buffer_1
  and and_1 (and_1_out, ~I_Oadr[3], ~I_Oadr[2], ~I_Oadr[1], I_Oadr[0], I_Osel);  // AND_Gate
  Decoder #(.disabled(0)) decoder_1 (.out0(decoder_1_out0), .out1(decoder_1_out1), .sel(in_out), .en(and_1_out));
endmodule

module DisplayReg2 (
  input  I_Osel,
  input  [3:0] I_Oadr,
  input  in_out,
  input  [3:0] I_Odat,
  output [3:0] out,
  output [3:0] value
);

  wire and_1_out, decoder_1_out0, decoder_1_out1;

  Register #(.width(4)) register_1 (.D(I_Odat), .Q(value), .clk(decoder_1_out0));  // open: en, clr
  assign out = decoder_1_out1 ? value : 4'bz;  // Controlled_Buffer controlled_buffer_1
  and and_1 (and_1_out, ~I_Oadr[3], ~I_Oadr[2], I_Oadr[1], ~I_Oadr[0], I_Osel);  // AND_Gate
  Decoder #(.disabled(0)) decoder_1 (.out0(decoder_1_out0), .out1(decoder_1_out1), .sel(in_out), .en(and_1_out));
endmodule

module DisplayReg3 (
  input  I_Osel,
  input  [3:0] I_Oadr,
  input  in_out,
  input  [3:0] I_Odat,
  output [3:0] out,
  output [3:0] value
);

  wire and_1_out, decoder_1_out0, decoder_1_out1;

  Register #(.width(4)) register_1 (.D(I_Odat), .Q(value), .clk(decoder_1_out0));  // open: en, clr
  assign out = decoder_1_out1 ? value : 4'bz;  // Controlled_Buffer controlled_buffer_1
  and and_1 (and_1_out, ~I_Oadr[3], ~I_Oadr[2], I_Oadr[1], I_Oadr[0], I_Osel);  // AND_Gate
  Decoder #(.disabled(0)) decoder_1 (.out0(decoder_1_out0), .out1(decoder_1_out1), .sel(in_out), .en(and_1_out));
endmodule

module DisplayReg4 (
  input  I_Osel,
  input  [3:0] I_Oadr,
  input  in_out,
  input  [3:0] I_Odat,
  output [3:0] out,
  output [3:0] value
);

  wire and_1_out, decoder_1_out0, decoder_1_out1;

  Register #(.width(4)) register_1 (.D(I_Odat), .Q(value), .clk(decoder_1_out0));  // open: en, clr
  assign out = decoder_1_out1 ? value : 4'bz;  // Controlled_Buffer controlled_buffer_1
  and and_1 (and_1_out, ~I_Oadr[3], I_Oadr[2], ~I_Oadr[1], ~I_Oadr[0], I_Osel);  // AND_Gate
  Decoder #(.disabled(0)) decoder_1 (.out0(decoder_1_out0), .out1(decoder_1_out1), .sel(in_out), .en(and_1_out));
endmodule

module DisplayReg5 (
  input  I_Osel,
  input  [3:0] I_Oadr,
  input  in_out,
  input  [3:0] I_Odat,
  output [3:0] out,
  output [3:0] value
);

  wire and_1_out, decoder_1_out0, decoder_1_out1;

  Register #(.width(4)) register_1 (.D(I_Odat), .Q(value), .clk(decoder_1_out0));  // open: en, clr
  assign out = decoder_1_out1 ? value : 4'bz;  // Controlled_Buffer controlled_buffer_1
  and and_1 (and_1_out, ~I_Oadr[3], I_Oadr[2], ~I_Oadr[1], I_Oadr[0], I_Osel);  // AND_Gate
  Decoder #(.disabled(0)) decoder_1 (.out0(decoder_1_out0), .out1(decoder_1_out1), .sel(in_out), .en(and_1_out));
endmodule

module DisplayReg6 (
  input  I_Osel,
  input  [3:0] I_Oadr,
  input  in_out,
  input  [3:0] I_Odat,
  output [3:0] out,
  output [3:0] value
);

  wire and_1_out, decoder_1_out0, decoder_1_out1;

  Register #(.width(4)) register_1 (.D(I_Odat), .Q(value), .clk(decoder_1_out0));  // open: en, clr
  assign out = decoder_1_out1 ? value : 4'bz;  // Controlled_Buffer controlled_buffer_1
  and and_1 (and_1_out, ~I_Oadr[3], I_Oadr[2], I_Oadr[1], ~I_Oadr[0], I_Osel);  // AND_Gate
  Decoder #(.disabled(0)) decoder_1 (.out0(decoder_1_out0), .out1(decoder_1_out1), .sel(in_out), .en(and_1_out));
endmodule

module DisplayReg7 (
  input  I_Osel,
  input  [3:0] I_Oadr,
  input  in_out,
  input  [3:0] I_Odat,
  output [3:0] out,
  output [3:0] value
);

  wire and_1_out, decoder_1_out0, decoder_1_out1;

  Register #(.width(4)) register_1 (.D(I_Odat), .Q(value), .clk(decoder_1_out0));  // open: en, clr
  assign out = decoder_1_out1 ? value : 4'bz;  // Controlled_Buffer controlled_buffer_1
  and and_1 (and_1_out, ~I_Oadr[3], I_Oadr[2], I_Oadr[1], I_Oadr[0], I_Osel);  // AND_Gate
  Decoder #(.disabled(0)) decoder_1 (.out0(decoder_1_out0), .out1(decoder_1_out1), .sel(in_out), .en(and_1_out));
endmodule

module DisplayReg8 (
  input  I_Osel,
  input  [3:0] I_Oadr,
  input  in_out,
  input  [3:0] I_Odat,
  output [3:0] out,
  output [3:0] value
);

  wire and_1_out, decoder_1_out0, decoder_1_out1;

  Register #(.width(4)) register_1 (.D(I_Odat), .Q(value), .clk(decoder_1_out0));  // open: en, clr
  assign out = decoder_1_out1 ? value : 4'bz;  // Controlled_Buffer controlled_buffer_1
  and and_1 (and_1_out, I_Oadr[3], ~I_Oadr[2], ~I_Oadr[1], ~I_Oadr[0], I_Osel);  // AND_Gate
  Decoder #(.disabled(0)) decoder_1 (.out0(decoder_1_out0), .out1(decoder_1_out1), .sel(in_out), .en(and_1_out));
endmodule

module DisplayReg9 (
  input  I_Osel,
  input  [3:0] I_Oadr,
  input  in_out,
  input  [3:0] I_Odat,
  output [3:0] out,
  output [3:0] value
);

  wire and_1_out, decoder_1_out0, decoder_1_out1;

  Register #(.width(4)) register_1 (.D(I_Odat), .Q(value), .clk(decoder_1_out0));  // open: en, clr
  assign out = decoder_1_out1 ? value : 4'bz;  // Controlled_Buffer controlled_buffer_1
  and and_1 (and_1_out, I_Oadr[3], ~I_Oadr[2], ~I_Oadr[1], I_Oadr[0], I_Osel);  // AND_Gate
  Decoder #(.disabled(0)) decoder_1 (.out0(decoder_1_out0), .out1(decoder_1_out1), .sel(in_out), .en(and_1_out));
endmodule

module PS_saver (
  input  I_O_sel,
  input  [3:0] I_O_Adr,
  input  in_out,
  input  [7:0] I_Odat,
  output [7:0] out
);

  wire and_1_out, decoder_1_out0, decoder_1_out1;
  wire [7:0] register_1_q;

  Register register_1 (.D(I_Odat), .Q(register_1_q), .clk(decoder_1_out0));  // open: en, clr
  assign out = decoder_1_out1 ? register_1_q : 8'bz;  // Controlled_Buffer controlled_buffer_1
  and and_1 (and_1_out, I_O_Adr[3], I_O_Adr[2], I_O_Adr[1], I_O_Adr[0], I_O_sel);
  Decoder #(.disabled(0)) decoder_1 (.out0(decoder_1_out0), .out1(decoder_1_out1), .sel(in_out), .en(and_1_out));
endmodule

module SP_saver (
  input  I_O_sel,
  input  [3:0] I_O_Adr,
  input  in_out,
  input  [7:0] I_Odat,
  output [7:0] out
);

  wire and_1_out, decoder_1_out0, decoder_1_out1;
  wire [7:0] register_1_q;

  Register register_1 (.D(I_Odat), .Q(register_1_q), .clk(decoder_1_out0));  // open: en, clr
  assign out = decoder_1_out1 ? register_1_q : 8'bz;  // Controlled_Buffer controlled_buffer_1
  and and_1 (and_1_out, I_O_Adr[3], I_O_Adr[2], I_O_Adr[1], ~I_O_Adr[0], I_O_sel);  // AND_Gate
  Decoder #(.disabled(0)) decoder_1 (.out0(decoder_1_out0), .out1(decoder_1_out1), .sel(in_out), .en(and_1_out));
endmodule

module Win_loose_screen (
  input  I_O_sel,
  input  [3:0] I_O_Adr,
  input  in_out,
  input  [7:0] I_Odat,
  output player,
  output Draw,
  output computer,
  output [7:0] I_Odat_2
);

  wire and_4_out, decoder_1_out0, decoder_1_out1;
  wire [7:0] register_1_q;

  and and_1 (player, register_1_q[0], register_1_q[1]);
  and and_2 (Draw, register_1_q[0], ~register_1_q[1]);  // AND_Gate
  and and_3 (computer, ~register_1_q[0], register_1_q[1]);  // AND_Gate
  assign I_Odat_2 = decoder_1_out1 ? register_1_q : 8'bz;  // Controlled_Buffer controlled_buffer_1
  Decoder #(.disabled(0)) decoder_1 (.out0(decoder_1_out0), .out1(decoder_1_out1), .sel(in_out), .en(and_4_out));
  Register register_1 (.D(I_Odat), .Q(register_1_q), .clk(decoder_1_out0));  // open: en, clr
  and and_4 (and_4_out, I_O_Adr[3], I_O_Adr[2], ~I_O_Adr[1], ~I_O_Adr[0], I_O_sel);  // AND_Gate

  // Notes on the sheet:
  //   Page number
endmodule
